# Fritzing sketch Circuit Diagram (saved by Fritzing 0.9.3b)
breadboards: 1

parts:
  DHT11_Temperature_&_Humidity_Sensor = Humidity and Temperature Sensor RHT03
  Part1 = Arduino Uno (Rev3)
  R1 = Resistor [tolerance=±5% resistance=4.7k package=THT]

nets:
  VCC: DHT11_Temperature_&_Humidity_Sensor.Vcc, Part1.5V, R1.Pin_0
  N1: DHT11_Temperature_&_Humidity_Sensor.Data-signal, Part1.D5_PWM, R1.Pin_1
  N2: DHT11_Temperature_&_Humidity_Sensor.GND_2, Part1.GND
